// Digital circuit ALU.dig as structural Verilog
module ALU (
  input  [31:0] A,
  input  [31:0] B,
  input  [2:0] Alu_op,
  output [31:0] res,
  output Cout,
  output isZero,
  output isLess
);

  wire c, c1;
  wire [31:0] s, s1, s2, s3, s4, s5;
  wire [63:32] mul_1_mul;

  Add #(.Bits(32)) add_1 (.a(A), .b(B), .c_i(1'b0), .s(s), .c_o(c));
  Sub #(.Bits(32)) sub_1 (.a(A), .b(B), .c_i(1'b0), .s(s1), .c_o(c1));
  Mul #(.Bits(32)) mul_1 (.a(A), .b(B), .mul({mul_1_mul, s2}));
  Div #(.Bits(32)) div_1 (.a(A), .b(B), .q(s3));  // open: r
  BarrelShifter #(.Bits(32)) barrelshifter_1 (.in(A), .shift(B[5:0]), .out(s4));
  BarrelShifter #(.Bits(32), .direction("right")) barrelshifter_2 (.in(A), .shift(B[5:0]), .out(s5));
  Multiplexer #(.Bits(32), .Selector_Bits(3)) multiplexer_1 (
    .sel(Alu_op), .in_0(s), .in_1(s1), .in_2(s2), .in_3(s3), .in_4(s4), .in_5(s5), .in_6(32'hfeedbeef),
    .in_7(32'hfeedbeef), .out(res));
  Multiplexer #(.Selector_Bits(3)) multiplexer_2 (
    .sel(Alu_op), .in_0(c), .in_1(c1), .in_2(1'b0), .in_3(1'b0), .in_4(1'b0), .in_5(1'b0), .in_6(1'b0),
    .in_7(1'b0), .out(Cout));
  Comparator #(.Bits(32), .Signed("true")) comparator_1 (
    .a(res), .b({32{1'b0}}), .eq(isZero), .lt(isLess));  // open: gt

  // Other names for the same wires on the sheet: op[2:0] = Alu_op
endmodule

/* Test case:
A B Alu_op res isZero isLess Cout
loop(x, 25)
	loop(y, 25)

let xx = x;
let yy = y;

let sum   = xx + yy;
let res   = xx - yy;
let mult  = xx * yy;
let div   = xx / (yy+1);
let sll   = xx << yy;
let srl   = xx >> yy;
let other = 0xFEEDBEEF;

(xx) (yy) 0 (sum)   (sum=0)   (sum<0)             (sum>>32)
(xx) (yy) 1 (res)   (res=0)   ((res<0)&(res>>32)) (res>>32)
(xx) (yy) 2 (mult)  (mult=0)  (mult<0)             X
(xx) (yy) 4 (sll)   (sll=0)   (sll<0)              X
(xx) (yy) 5 (srl)   (srl=0)   (srl<0)              X
(xx) (yy) 6 (other) (other=0)    1                X
(xx) (yy) 7 (other) (other=0)    1                X

	end loop
end loop
*/
