// Digital circuit divcircuit.dig as structural Verilog
module divcircuit (
  input  [3:0] m,
  input  [3:0] a,
  input  [3:0] q,
  output [3:0] aa,
  output [3:0] qq
);

  wire com;
  wire [3:0] q_t, sub_1_s;
  wire [7:4] barrelshifter_1_out;

  BarrelShifter #(.Bits(8)) barrelshifter_1 (.in({a, q}), .shift(4'b0001), .out({barrelshifter_1_out, q_t}));
  Sub #(.Bits(4)) sub_1 (.a(barrelshifter_1_out), .b(m), .c_i(1'b0), .s(sub_1_s), .c_o(com));
  Multiplexer #(.Bits(4)) multiplexer_1 (.sel(com), .in_0(sub_1_s), .in_1(barrelshifter_1_out), .out(aa));
  Multiplexer #(.Bits(4)) multiplexer_2 (.sel(com), .in_0({q_t[3:1], 1'b1}), .in_1({q_t[3:1], 1'b0}), .out(qq));
endmodule
