// Digital circuit divisor.dig as structural Verilog
module divisor (
  input  [3:0] divisor,
  input  [3:0] dividend,
  output [3:0] r,
  output [3:0] q
);

  wire [3:0] divcircuit_1_aa, divcircuit_1_qq, divcircuit_2_aa, divcircuit_2_qq, divcircuit_3_aa,
       divcircuit_3_qq;

  divcircuit divcircuit_1 (.m(divisor), .a(4'b0000), .q(dividend), .aa(divcircuit_1_aa), .qq(divcircuit_1_qq));
  divcircuit divcircuit_2 (
    .m(divisor), .a(divcircuit_1_aa), .q(divcircuit_1_qq), .aa(divcircuit_2_aa), .qq(divcircuit_2_qq));
  divcircuit divcircuit_3 (
    .m(divisor), .a(divcircuit_2_aa), .q(divcircuit_2_qq), .aa(divcircuit_3_aa), .qq(divcircuit_3_qq));
  divcircuit divcircuit_4 (.m(divisor), .a(divcircuit_3_aa), .q(divcircuit_3_qq), .aa(r), .qq(q));
endmodule

/* Test case:
divisor dividend q r
loop(x, 14)
	loop(y, 15)
let xP = x + 1;
(xP) (y) (y/xP) (y%xP)
	end loop
end loop
*/
